# Fritzing sketch ArduinoAndProcessingGame_Fritzing_Trives_Pelayo (saved by Fritzing 0.9.6b)
breadboards: 1

parts:
  Componente1 = Arduino Uno (Rev3)
  LED1 = LED - 5mm [color="Blue (525nm)" current=0.030 package="5 mm [THT]"]
  LED2 = LED - 5mm [color="Red (633nm)" current=0.030 package="5 mm [THT]"]
  LED3 = LED - 5mm [color="Green (565nm)" current=0.030 package="5 mm [THT]"]
  R1 = Resistor [tolerance=±5% power=0.25 resistance=220 package=THT]
  R2 = Resistor [tolerance=±5% power=0.25 resistance=220 package=THT]
  R3 = Resistor [tolerance=±5% power=0.25 resistance=220 package=THT]
  S1 = Pushbutton [package="[THT]"]
  S2 = Pushbutton [package="[THT]"]
  R4 = Resistor [tolerance=±5% power=0.25 resistance=4.7k package=THT]
  R5 = Resistor [tolerance=±5% power=0.25 resistance=4.7k package=THT]
  R6 = Rotary Potentiometer (Large) [maximum_resistance=100kΩ package=THT]

nets:
  N1: Componente1.A0, R6.wiper
  N2: Componente1.D8, R3.Pin_1
  N3: Componente1.D9_PWM, R2.Pin_1
  N4: Componente1.D10_PWM/SS, R1.Pin_1
  N5: Componente1.D2, S2.Pin_3, S2.Pin_4, R5.Pin_0
  N6: Componente1.D4, S1.Pin_3, S1.Pin_4, R4.Pin_0
  N7: Componente1.5V, R4.Pin_1, R5.Pin_1, R6.leg2
  N8: Componente1.GND, LED1.cathode, LED2.cathode, LED3.cathode, S1.Pin_1, S1.Pin_2, S2.Pin_1, S2.Pin_2, R6.leg1
  N9: LED1.anode, R1.Pin_0
  N10: LED2.anode, R2.Pin_0
  N11: LED3.anode, R3.Pin_0
